# Fritzing sketch 02-BlinkingTheLEDWithUWP (saved by Fritzing 0.9.2b)
breadboards: 1

parts:
  Raspberry_Pi1 = Raspberry Pi 2
  S1 = Round Pushbutton
  LED1 = smd LED [color="Red (633nm)" package="0603 [SMD]"]
  R1 = Resistor [tolerance=±5% resistance=330 package=THT]

nets:
  N1: Raspberry_Pi1.3v3, R1.Pin_1
  N2: Raspberry_Pi1.GND, S1.leg1
  N3: Raspberry_Pi1.GPIO5, LED1.cathode
  N4: Raspberry_Pi1.GPIO6, S1.leg0
  N5: LED1.anode, R1.Pin_0
