# Fritzing sketch 03-WorkingWithAnalogSensors (saved by Fritzing 0.9.2b)
breadboards: 1

parts:
  Raspberry_Pi1 = Raspberry Pi 2
  S1 = Round Pushbutton
  LED1 = smd LED [color="Red (633nm)" package="0603 [SMD]"]
  R1 = Resistor [tolerance=±5% resistance=330 package=THT]
  IC1 = MCP3008 8-channel 10-bit ADC [part_number=MCP3008]
  R2 = PHOTOCELL [package=photocell]
  R3 = Resistor [tolerance=±5% resistance=10k package=THT]

nets:
  N1: Raspberry_Pi1.3v3, R1.Pin_1, IC1.no_name_yet#15, IC1.no_name_yet#16, R3.Pin_0
  N2: Raspberry_Pi1.GND, S1.leg1, IC1.no_name_yet#9, IC1.no_name_yet#14, R2.P$2
  N3: Raspberry_Pi1.GPIO10, IC1.no_name_yet#11
  N4: Raspberry_Pi1.GPIO9, IC1.no_name_yet#12
  N5: Raspberry_Pi1.GPIO11, IC1.no_name_yet#13
  N6: Raspberry_Pi1.GPIO5, LED1.cathode
  N7: Raspberry_Pi1.GPIO6, S1.leg0
  N8: Raspberry_Pi1.GPIO8, IC1.no_name_yet#10
  N9: LED1.anode, R1.Pin_0
  N10: IC1.no_name_yet#1, R2.P$1, R3.Pin_1
